// Digital circuit arithmetic.dig as structural Verilog
module arithmetic (
  input  [7:0] alu__a,
  input  [7:0] alu__b,
  input  alu__negb,
  input  alu__and,
  input  alu__or,
  input  alu__xor,
  input  alu__rot,
  input  alu__cin,
  input  alu__add,
  output [7:0] alu__y,
  output alu__z,
  output alu__cout,
  output alu__n,
  output alu__v
);

  wire add_1_c_o, xnor_1_out, xnor_2_out;
  wire [7:0] add_1_s, and_1_out, multiplexer_1_out, multiplexer_2_out, multiplexer_3_out, multiplexer_4_out,
       multiplexer_5_out, not_1_out, or_1_out, xor_1_out;

  assign not_1_out = ~alu__b;  // Not not_1, 8 bits wide
  Multiplexer #(.Bits(8)) multiplexer_1 (.sel(alu__negb), .in_0(alu__b), .in_1(not_1_out), .out(multiplexer_1_out));
  assign and_1_out = alu__a & multiplexer_1_out;  // And and_1, 8 bits wide
  assign or_1_out = alu__a | multiplexer_1_out;  // Or or_1, 8 bits wide
  Multiplexer #(.Bits(8)) multiplexer_2 (.sel(alu__and), .in_0({8{1'b0}}), .in_1(and_1_out), .out(multiplexer_2_out));
  Multiplexer #(.Bits(8)) multiplexer_3 (
    .sel(alu__or), .in_0(multiplexer_2_out), .in_1(or_1_out), .out(multiplexer_3_out));
  assign xor_1_out = alu__a ^ multiplexer_1_out;  // XOr xor_1, 8 bits wide
  Multiplexer #(.Bits(8)) multiplexer_4 (
    .sel(alu__xor), .in_0(multiplexer_3_out), .in_1(xor_1_out), .out(multiplexer_4_out));
  Multiplexer #(.Bits(8)) multiplexer_5 (
    .sel(alu__rot), .in_0(multiplexer_4_out), .in_1({alu__cin, alu__a[7:1]}), .out(multiplexer_5_out));
  xnor xnor_1 (xnor_1_out, alu__a[7], multiplexer_1_out[7]);
  xnor xnor_2 (xnor_2_out, multiplexer_1_out[7], alu__n);
  Add #(.Bits(8)) add_1 (.a(alu__a), .b(multiplexer_1_out), .c_i(alu__cin), .s(add_1_s), .c_o(add_1_c_o));
  Multiplexer #(.Bits(8)) multiplexer_6 (
    .sel(alu__add), .in_0(multiplexer_5_out), .in_1(add_1_s), .out({alu__n, alu__y[6:0]}));
  Comparator #(.Bits(8)) comparator_1 (.a({alu__n, alu__y[6:0]}), .b({8{1'b0}}), .eq(alu__z));  // open: gt, lt
  or or_2 (alu__cout, alu__a[0], add_1_c_o);
  and and_2 (alu__v, xnor_1_out, xnor_2_out);

  assign alu__y[7] = alu__n;

  // Other names for the same wires on the sheet: cin = alu__cin; y[7:0] = {alu__n, alu__y[6:0]}
endmodule
