// Digital circuit control.dig as structural Verilog
module control (
  input  [1:0] ctl__stage,
  input  [3:0] ctl__op,
  output ctl__op__halt,
  output ctl__op__add,
  output ctl__op__adc,
  output ctl__op__sub,
  output ctl__op__sbb,
  output ctl__op__and,
  output ctl__op__or,
  output ctl__op__xor,
  output ctl__op__rrc,
  output ctl__op__set,
  output ctl__op__lw,
  output ctl__op__sw,
  output ctl__op__rsr,
  output ctl__op__wsr,
  output ctl__op__jal,
  output ctl__op__jmp
);

  wire decoder_1_out_0, decoder_1_out_1, decoder_1_out_2, decoder_1_out_3, decoder_1_out_4, decoder_1_out_5,
       decoder_1_out_6, decoder_1_out_7, decoder_1_out_8, decoder_1_out_9, decoder_1_out_10,
       decoder_1_out_11, decoder_1_out_12, decoder_1_out_13, decoder_1_out_14, decoder_1_out_15,
       stage__execute, stage__fetchhi, stage__fetchlo;

  Demultiplexer #(.Selector_Bits(2)) demultiplexer_1 (
    .sel(ctl__stage), .in(1'b1), .out_0(stage__fetchlo), .out_1(stage__fetchhi), .out_2(stage__execute));  // open: out_3
  Decoder #(.Selector_Bits(4)) decoder_1 (
    .sel(ctl__op), .out_0(decoder_1_out_0), .out_1(decoder_1_out_1), .out_2(decoder_1_out_2),
    .out_3(decoder_1_out_3), .out_4(decoder_1_out_4), .out_5(decoder_1_out_5), .out_6(decoder_1_out_6),
    .out_7(decoder_1_out_7), .out_8(decoder_1_out_8), .out_9(decoder_1_out_9), .out_10(decoder_1_out_10),
    .out_11(decoder_1_out_11), .out_12(decoder_1_out_12), .out_13(decoder_1_out_13),
    .out_14(decoder_1_out_14), .out_15(decoder_1_out_15));
  and and_1 (ctl__op__halt, decoder_1_out_0, stage__execute);
  and and_2 (ctl__op__add, decoder_1_out_1, stage__execute);
  and and_3 (ctl__op__adc, decoder_1_out_2, stage__execute);
  and and_4 (ctl__op__sub, decoder_1_out_3, stage__execute);
  and and_5 (ctl__op__sbb, decoder_1_out_4, stage__execute);
  and and_6 (ctl__op__and, decoder_1_out_5, stage__execute);
  and and_7 (ctl__op__or, decoder_1_out_6, stage__execute);
  and and_8 (ctl__op__xor, decoder_1_out_7, stage__execute);
  and and_9 (ctl__op__rrc, decoder_1_out_8, stage__execute);
  and and_10 (ctl__op__set, decoder_1_out_9, stage__execute);
  and and_11 (ctl__op__lw, decoder_1_out_10, stage__execute);
  and and_12 (ctl__op__sw, decoder_1_out_11, stage__execute);
  and and_13 (ctl__op__rsr, decoder_1_out_12, stage__execute);
  and and_14 (ctl__op__wsr, decoder_1_out_13, stage__execute);
  and and_15 (ctl__op__jal, decoder_1_out_14, stage__execute);
  and and_16 (ctl__op__jmp, decoder_1_out_15, stage__execute);
endmodule
