// Digital circuit misa.dig as structural Verilog
module misa (
);

  wire decoder_1_p1, decoder_1_p2, decoder_1_p3, regfile_1_p1, regfile_1_p5;
  wire [7:0] decoder_1_p4, multiplexer_1_out, regfile_1_p6;

  // decoder decoder_1: pin names not known; wires that end beside it: decoder_1_p1, decoder_1_p2, decoder_1_p3, decoder_1_p4
  // regfile regfile_1: pin names not known; wires that end beside it: regfile_1_p1, decoder_1_p1, decoder_1_p2, decoder_1_p3, regfile_1_p5, regfile_1_p6
  Multiplexer #(.Bits(8)) multiplexer_1 (
    .in_0(regfile_1_p6), .in_1(decoder_1_p4), .out(multiplexer_1_out));  // open: sel
  // arithmetic arithmetic_1: pin names not known; wires that end beside it: regfile_1_p5, multiplexer_1_out, regfile_1_p1
endmodule
