// Digital circuit regfile.dig as structural Verilog
module regfile (
  input  [3:0] reg__port1,
  input  [3:0] reg__port2,
  input  [3:0] reg__port3,
  input  reg__port1__write,
  input  reg__port2__write,
  input  reg__clk,
  output [7:0] reg__port1__data,
  output [7:0] reg__port2__data,
  output [7:0] reg__port3__data
);

  wire demultiplexer_1_out_1, demultiplexer_1_out_2, demultiplexer_1_out_3, demultiplexer_1_out_4,
       demultiplexer_1_out_5, demultiplexer_1_out_6, demultiplexer_1_out_7, demultiplexer_1_out_8,
       demultiplexer_1_out_9, demultiplexer_1_out_10, demultiplexer_1_out_11, demultiplexer_1_out_12,
       demultiplexer_1_out_13, demultiplexer_1_out_14, demultiplexer_1_out_15, demultiplexer_2_out_1,
       demultiplexer_2_out_2, demultiplexer_2_out_3, demultiplexer_2_out_4, demultiplexer_2_out_5,
       demultiplexer_2_out_6, demultiplexer_2_out_7, demultiplexer_2_out_8, demultiplexer_2_out_9,
       demultiplexer_2_out_10, demultiplexer_2_out_11, demultiplexer_2_out_12, demultiplexer_2_out_13,
       demultiplexer_2_out_14, demultiplexer_2_out_15, not_1_out, not_2_out, or_1_out, or_2_out, or_3_out,
       or_4_out, or_5_out, or_6_out, or_7_out, or_8_out, or_9_out, or_10_out, or_11_out, or_12_out,
       or_13_out, or_14_out, or_15_out;
  wire [7:0] port1__data_out, port2__data_out, register_1_q, register_2_q, register_3_q, register_4_q,
       register_5_q, register_6_q, register_7_q, register_8_q, register_9_q, register_10_q, register_11_q,
       register_12_q, register_13_q, register_14_q, register_15_q, write__data;

  Multiplexer #(.Bits(8)) multiplexer_1 (
    .sel(reg__port1__write), .in_0(reg__port2__data), .in_1(reg__port1__data), .out(write__data));
  Demultiplexer #(.Selector_Bits(4)) demultiplexer_1 (
    .sel(reg__port1), .in(reg__port1__write), .out_1(demultiplexer_1_out_1), .out_2(demultiplexer_1_out_2),
    .out_3(demultiplexer_1_out_3), .out_4(demultiplexer_1_out_4), .out_5(demultiplexer_1_out_5),
    .out_6(demultiplexer_1_out_6), .out_7(demultiplexer_1_out_7), .out_8(demultiplexer_1_out_8),
    .out_9(demultiplexer_1_out_9), .out_10(demultiplexer_1_out_10), .out_11(demultiplexer_1_out_11),
    .out_12(demultiplexer_1_out_12), .out_13(demultiplexer_1_out_13), .out_14(demultiplexer_1_out_14),
    .out_15(demultiplexer_1_out_15));  // open: out_0
  Demultiplexer #(.Selector_Bits(4)) demultiplexer_2 (
    .sel(reg__port2), .in(reg__port2__write), .out_1(demultiplexer_2_out_1), .out_2(demultiplexer_2_out_2),
    .out_3(demultiplexer_2_out_3), .out_4(demultiplexer_2_out_4), .out_5(demultiplexer_2_out_5),
    .out_6(demultiplexer_2_out_6), .out_7(demultiplexer_2_out_7), .out_8(demultiplexer_2_out_8),
    .out_9(demultiplexer_2_out_9), .out_10(demultiplexer_2_out_10), .out_11(demultiplexer_2_out_11),
    .out_12(demultiplexer_2_out_12), .out_13(demultiplexer_2_out_13), .out_14(demultiplexer_2_out_14),
    .out_15(demultiplexer_2_out_15));  // open: out_0
  or or_1 (or_1_out, demultiplexer_1_out_1, demultiplexer_2_out_1);
  or or_2 (or_2_out, demultiplexer_1_out_2, demultiplexer_2_out_2);
  or or_3 (or_3_out, demultiplexer_1_out_3, demultiplexer_2_out_3);
  or or_4 (or_4_out, demultiplexer_1_out_4, demultiplexer_2_out_4);
  or or_5 (or_5_out, demultiplexer_1_out_5, demultiplexer_2_out_5);
  or or_6 (or_6_out, demultiplexer_1_out_6, demultiplexer_2_out_6);
  or or_7 (or_7_out, demultiplexer_1_out_7, demultiplexer_2_out_7);
  or or_8 (or_8_out, demultiplexer_1_out_8, demultiplexer_2_out_8);
  or or_9 (or_9_out, demultiplexer_1_out_9, demultiplexer_2_out_9);
  or or_10 (or_10_out, demultiplexer_1_out_10, demultiplexer_2_out_10);
  or or_11 (or_11_out, demultiplexer_1_out_11, demultiplexer_2_out_11);
  or or_12 (or_12_out, demultiplexer_1_out_12, demultiplexer_2_out_12);
  or or_13 (or_13_out, demultiplexer_1_out_13, demultiplexer_2_out_13);
  or or_14 (or_14_out, demultiplexer_1_out_14, demultiplexer_2_out_14);
  or or_15 (or_15_out, demultiplexer_1_out_15, demultiplexer_2_out_15);
  Register #(.Bits(8)) register_1 (.D(write__data), .C(reg__clk), .en(or_1_out), .Q(register_1_q));
  Register #(.Bits(8)) register_2 (.D(write__data), .C(reg__clk), .en(or_2_out), .Q(register_2_q));
  Register #(.Bits(8)) register_3 (.D(write__data), .C(reg__clk), .en(or_3_out), .Q(register_3_q));
  Register #(.Bits(8)) register_4 (.D(write__data), .C(reg__clk), .en(or_4_out), .Q(register_4_q));
  Register #(.Bits(8)) register_5 (.D(write__data), .C(reg__clk), .en(or_5_out), .Q(register_5_q));
  Register #(.Bits(8)) register_6 (.D(write__data), .C(reg__clk), .en(or_6_out), .Q(register_6_q));
  Register #(.Bits(8)) register_7 (.D(write__data), .C(reg__clk), .en(or_7_out), .Q(register_7_q));
  Register #(.Bits(8)) register_8 (.D(write__data), .C(reg__clk), .en(or_8_out), .Q(register_8_q));
  Register #(.Bits(8)) register_9 (.D(write__data), .C(reg__clk), .en(or_9_out), .Q(register_9_q));
  Register #(.Bits(8)) register_10 (.D(write__data), .C(reg__clk), .en(or_10_out), .Q(register_10_q));
  Register #(.Bits(8)) register_11 (.D(write__data), .C(reg__clk), .en(or_11_out), .Q(register_11_q));
  Register #(.Bits(8)) register_12 (.D(write__data), .C(reg__clk), .en(or_12_out), .Q(register_12_q));
  Register #(.Bits(8)) register_13 (.D(write__data), .C(reg__clk), .en(or_13_out), .Q(register_13_q));
  Register #(.Bits(8)) register_14 (.D(write__data), .C(reg__clk), .en(or_14_out), .Q(register_14_q));
  Register #(.Bits(8)) register_15 (.D(write__data), .C(reg__clk), .en(or_15_out), .Q(register_15_q));
  Multiplexer #(.Selector_Bits(4), .Bits(8)) multiplexer_2 (
    .sel(reg__port1), .in_0({8{1'b0}}), .in_1(register_1_q), .in_2(register_2_q), .in_3(register_3_q),
    .in_4(register_4_q), .in_5(register_5_q), .in_6(register_6_q), .in_7(register_7_q), .in_8(register_8_q),
    .in_9(register_9_q), .in_10(register_10_q), .in_11(register_11_q), .in_12(register_12_q),
    .in_13(register_13_q), .in_14(register_14_q), .in_15(register_15_q), .out(port1__data_out));
  Multiplexer #(.Selector_Bits(4), .Bits(8)) multiplexer_3 (
    .sel(reg__port2), .in_0({8{1'b0}}), .in_1(register_1_q), .in_2(register_2_q), .in_3(register_3_q),
    .in_4(register_4_q), .in_5(register_5_q), .in_6(register_6_q), .in_7(register_7_q), .in_8(register_8_q),
    .in_9(register_9_q), .in_10(register_10_q), .in_11(register_11_q), .in_12(register_12_q),
    .in_13(register_13_q), .in_14(register_14_q), .in_15(register_15_q), .out(port2__data_out));
  Multiplexer #(.Selector_Bits(4), .Bits(8)) multiplexer_4 (
    .sel(reg__port3), .in_0({8{1'b0}}), .in_1(register_1_q), .in_2(register_2_q), .in_3(register_3_q),
    .in_4(register_4_q), .in_5(register_5_q), .in_6(register_6_q), .in_7(register_7_q), .in_8(register_8_q),
    .in_9(register_9_q), .in_10(register_10_q), .in_11(register_11_q), .in_12(register_12_q),
    .in_13(register_13_q), .in_14(register_14_q), .in_15(register_15_q), .out(reg__port3__data));
  not not_1 (not_1_out, reg__port1__write);
  assign reg__port1__data = not_1_out ? port1__data_out : 8'bz;  // Driver driver_1
  not not_2 (not_2_out, reg__port2__write);
  assign reg__port2__data = not_2_out ? port2__data_out : 8'bz;  // Driver driver_2

  // Other names for the same wires on the sheet: port1[3:0] = reg__port1; port1__data_in[7:0] = reg__port1__data;
  //   port1__write = reg__port1__write; port2[3:0] = reg__port2; port2__data_in[7:0] = reg__port2__data;
  //   port2__write = reg__port2__write; port3[3:0] = reg__port3; port3__data[7:0] = reg__port3__data
endmodule
