// Digital circuit comparator.dig as structural Verilog
module comparator (
  input  [15:0] cmp__flags,
  output cmp__always,
  output cmp__equal,
  output cmp__not__equal,
  output cmp__greater,
  output cmp__less,
  output cmp__greater__equal,
  output cmp__less__equal
);

  wire or_1_out, xor_1_out, xor_2_out, xor_3_out;

  xor xor_1 (xor_1_out, cmp__flags[2], cmp__flags[3]);
  or or_1 (or_1_out, xor_1_out, cmp__flags[0]);
  xor xor_2 (xor_2_out, cmp__flags[2], cmp__flags[3]);
  xor xor_3 (xor_3_out, cmp__flags[2], cmp__flags[3]);
  xor xor_4 (cmp__less, cmp__flags[2], cmp__flags[3]);
  or or_2 (cmp__less__equal, xor_3_out, cmp__flags[0]);
  not not_1 (cmp__not__equal, cmp__flags[0]);
  not not_2 (cmp__greater, or_1_out);
  not not_3 (cmp__greater__equal, xor_2_out);

  assign cmp__always = 1'b1;
  assign cmp__equal = cmp__flags[0];

  // Other names for the same wires on the sheet: z = cmp__flags[0]; c = cmp__flags[1]; n = cmp__flags[2];
  //   v = cmp__flags[3]
endmodule
