// Digital circuit control.dig as structural Verilog
module control (
  input  [1:0] ctl__stage,
  input  [3:0] ctl__op,
  input  ctl__loading__pc,
  output ctl__op__halt,
  output ctl__op__add,
  output ctl__op__adc,
  output ctl__op__sub,
  output ctl__op__sbb,
  output ctl__op__and,
  output ctl__op__or,
  output ctl__op__xor,
  output ctl__op__rrc,
  output ctl__op__set,
  output ctl__op__ld,
  output ctl__op__st,
  output ctl__op__rsr,
  output ctl__op__wsr,
  output ctl__op__jal,
  output ctl__op__jmp,
  output ctl__port1__write,
  output ctl__port2__write,
  output ctl__negb,
  output ctl__add,
  output ctl__mem__wrback,
  output ctl__mem__rdinst,
  output ctl__mem__read,
  output ctl__mem__write,
  output ctl__use__imm,
  output ctl__use__port1,
  output ctl__use__port2,
  output ctl__use__port3,
  output ctl__wrflags,
  output ctl__branch,
  output ctl__load__pc,
  output ctl__keep__loading__pc
);

  wire and_1_out, decoder_1_out_0, decoder_1_out_1, decoder_1_out_2, decoder_1_out_3, decoder_1_out_4,
       decoder_1_out_5, decoder_1_out_6, decoder_1_out_7, decoder_1_out_8, decoder_1_out_9, decoder_1_out_10,
       decoder_1_out_11, decoder_1_out_12, decoder_1_out_13, decoder_1_out_14, decoder_1_out_15,
       stage__execute, stage__fetchhi, stage__fetchlo;

  Demultiplexer #(.Selector_Bits(2)) demultiplexer_1 (
    .sel(ctl__stage), .in(1'b1), .out_0(stage__fetchlo), .out_1(stage__fetchhi), .out_2(stage__execute));  // open: out_3
  Decoder #(.Selector_Bits(4)) decoder_1 (
    .sel(ctl__op), .out_0(decoder_1_out_0), .out_1(decoder_1_out_1), .out_2(decoder_1_out_2),
    .out_3(decoder_1_out_3), .out_4(decoder_1_out_4), .out_5(decoder_1_out_5), .out_6(decoder_1_out_6),
    .out_7(decoder_1_out_7), .out_8(decoder_1_out_8), .out_9(decoder_1_out_9), .out_10(decoder_1_out_10),
    .out_11(decoder_1_out_11), .out_12(decoder_1_out_12), .out_13(decoder_1_out_13),
    .out_14(decoder_1_out_14), .out_15(decoder_1_out_15));
  and and_1 (and_1_out, stage__execute, ~ctl__loading__pc);  // And
  and and_2 (ctl__op__halt, decoder_1_out_0, and_1_out);
  and and_3 (ctl__op__add, decoder_1_out_1, and_1_out);
  and and_4 (ctl__op__adc, decoder_1_out_2, and_1_out);
  and and_5 (ctl__op__sub, decoder_1_out_3, and_1_out);
  and and_6 (ctl__op__sbb, decoder_1_out_4, and_1_out);
  and and_7 (ctl__op__and, decoder_1_out_5, and_1_out);
  and and_8 (ctl__op__or, decoder_1_out_6, and_1_out);
  and and_9 (ctl__op__xor, decoder_1_out_7, and_1_out);
  and and_10 (ctl__op__rrc, decoder_1_out_8, and_1_out);
  and and_11 (ctl__op__set, decoder_1_out_9, and_1_out);
  and and_12 (ctl__mem__wrback, decoder_1_out_10, and_1_out);
  and and_13 (ctl__mem__write, decoder_1_out_11, and_1_out);
  and and_14 (ctl__op__rsr, decoder_1_out_12, and_1_out);
  and and_15 (ctl__op__wsr, decoder_1_out_13, and_1_out);
  and and_16 (ctl__op__jal, decoder_1_out_14, and_1_out);
  and and_17 (ctl__op__jmp, decoder_1_out_15, and_1_out);
  or or_1 (ctl__port1__write, ctl__op__add, ctl__op__adc, ctl__op__sub, ctl__op__sbb, ctl__op__and, ctl__op__or, ctl__op__xor, ctl__op__rrc, ctl__op__set, ctl__mem__wrback, ctl__op__rsr);
  or or_2 (ctl__negb, ctl__op__sub, ctl__op__sbb);
  or or_3 (ctl__add, ctl__op__add, ctl__op__adc, ctl__op__sub, ctl__op__sbb, ctl__op__set);
  or or_4 (ctl__mem__rdinst, stage__fetchlo, stage__fetchhi);
  or or_5 (ctl__mem__read, stage__fetchlo, stage__fetchhi, ctl__mem__wrback);
  or or_6 (ctl__use__port2, ctl__op__add, ctl__op__adc, ctl__op__sub, ctl__op__sbb, ctl__op__and, ctl__op__or, ctl__op__xor, ctl__op__rrc, ctl__mem__wrback, ctl__mem__write, ctl__op__rsr, ctl__op__wsr, ctl__op__jal, ctl__op__jmp);
  or or_7 (ctl__use__port3, ctl__op__add, ctl__op__adc, ctl__op__sub, ctl__op__sbb, ctl__op__and, ctl__op__or, ctl__op__xor, ctl__mem__wrback, ctl__mem__write);
  or or_8 (ctl__wrflags, ctl__op__add, ctl__op__adc, ctl__op__sub, ctl__op__sbb);
  or or_9 (ctl__branch, ctl__op__jal, ctl__op__jmp);
  and and_18 (ctl__load__pc, ctl__loading__pc, stage__execute);
  and and_19 (ctl__keep__loading__pc, ctl__loading__pc, ~stage__execute);  // And

  assign ctl__op__ld = ctl__mem__wrback;
  assign ctl__op__st = ctl__mem__write;
  assign ctl__port2__write = ctl__op__rsr;
  assign ctl__use__imm = ctl__op__set;
  assign ctl__use__port1 = 1'b1;
endmodule
