// Digital circuit decoder.dig as structural Verilog
module decoder (
  input  [15:0] dec__inst,
  output [3:0] dec__op,
  output [3:0] dec__rd,
  output [3:0] dec__rs1,
  output [3:0] dec__rs2,
  output [7:0] dec__imm,
  output [3:0] dec__csr,
  output [3:0] dec__cmp
);


  assign dec__cmp = dec__inst[15:12];
  assign dec__csr = dec__inst[15:12];
  assign dec__imm = dec__inst[15:8];
  assign dec__op = dec__inst[3:0];
  assign dec__rd = dec__inst[7:4];
  assign dec__rs1 = dec__inst[11:8];
  assign dec__rs2 = dec__inst[15:12];
endmodule
