// Digital circuit csrfile.dig as structural Verilog
module csrfile (
  input  [15:0] csr__saddr__in,
  input  [15:0] csr__raddr__in,
  input  [15:0] csr__flags__in,
  input  [15:0] csr__cause__in,
  input  csr__saddr__write,
  input  csr__raddr__write,
  input  csr__flags__write,
  input  csr__cause__write,
  input  csr__clk,
  output [15:0] csr__saddr__out,
  output [15:0] csr__raddr__out,
  output [15:0] csr__flags__out,
  output [15:0] csr__cause__out,
  output [15:0] csr__extns__out
);

  Register #(.Bits(16)) register_1 (.D(csr__saddr__in), .C(csr__clk), .en(csr__saddr__write), .Q(csr__saddr__out));
  Register #(.Bits(16)) register_2 (.D(csr__raddr__in), .C(csr__clk), .en(csr__raddr__write), .Q(csr__raddr__out));
  Register #(.Bits(16)) register_3 (.D(csr__flags__in), .C(csr__clk), .en(csr__flags__write), .Q(csr__flags__out));
  Register #(.Bits(16)) register_4 (.D(csr__cause__in), .C(csr__clk), .en(csr__cause__write), .Q(csr__cause__out));

  assign csr__extns__out = {16{1'b0}};
endmodule
