// Digital circuit memory.dig as structural Verilog
module memory (
  input  [7:0] mem__write__data,
  input  [15:0] mem__addr,
  input  mem__read,
  input  mem__write,
  input  mem__clk,
  output [7:0] mem__read__data,
  output mem__ready
);

  RAMDualPort #(.AddrBits(16), .isProgramMemory("true"), .Bits(8)) ramdualport_1 (
    .A(mem__addr), .Din(mem__write__data), .str(mem__write), .C(mem__clk), .ld(mem__read), .D(mem__read__data));
  or or_1 (mem__ready, mem__write, mem__read);
endmodule
