// Digital circuit misa.dig as structural Verilog
module misa (
  input  Clock,
  input  Reset
);

  wire alu__cout, alu__n, alu__v, alu__z, and_1_out, and_2_out, and_3_out, and_4_out, and_5_out, clk,
       cmp__branch, comparator_1_cmp__always, comparator_1_cmp__equal, comparator_1_cmp__greater,
       comparator_1_cmp__greater__equal, comparator_1_cmp__less, comparator_1_cmp__less__equal,
       comparator_1_cmp__not__equal, ctl__add, ctl__branch, ctl__mem__rdinst, ctl__mem__read,
       ctl__mem__wrback, ctl__mem__write, ctl__negb, ctl__op__adc, ctl__op__add, ctl__op__and, ctl__op__halt,
       ctl__op__jal, ctl__op__jmp, ctl__op__lw, ctl__op__or, ctl__op__rcc, ctl__op__rsr, ctl__op__sbb,
       ctl__op__set, ctl__op__sub, ctl__op__sw, ctl__op__wsr, ctl__op__xor, ctl__port1__write,
       ctl__port2__write, ctl__use__imm, ctl__use__port1, ctl__use__port2, ctl__use__port3, ctl__wrflags,
       demultiplexer_1_out_1, demultiplexer_1_out_2, demultiplexer_1_out_3, demultiplexer_1_out_4, flags__c,
       halt, jk_ff_1_q, jk_ff_2_nq, multiplexer_15_out, multiplexer_16_out, multiplexer_18_out, not_1_out,
       not_2_out, or_1_out, or_2_out, or_3_out, rs_ff_as_1_q, stage__execute, stage__fetch, stage__fetchhi,
       stage__fetchlo;
  wire [1:0] stage;
  wire [3:0] decoder_1_dec__cmp, decoder_1_dec__csr, decoder_1_dec__op, decoder_1_dec__rd,
       decoder_1_dec__rs1, decoder_1_dec__rs2, multiplexer_4_out, multiplexer_5_out, multiplexer_6_out;
  wire [7:0] alu__y, decoder_1_dec__imm, demultiplexer_2_out_0, demultiplexer_2_out_1, mem__read__data,
       multiplexer_7_out, multiplexer_11_out, reg__port1__data_in___alu, reg__port1__data_in___rsr,
       reg__port1__data_out, reg__port2__data_in, reg__port2__data_out, reg__port3__data;
  wire [15:0] csrfile_1_csr__cause__out, csrfile_1_csr__flags__out, csrfile_1_csr__raddr__out,
       csrfile_1_csr__saddr__out, hw__cause, inst, multiplexer_1_out, multiplexer_2_out, multiplexer_3_out,
       multiplexer_10_out, multiplexer_12_out, multiplexer_14_out, multiplexer_20_out, next__pc, pc;

  Demultiplexer #(.Selector_Bits(4)) demultiplexer_1 (
    .sel(decoder_1_dec__csr), .in(1'b1), .out_1(demultiplexer_1_out_1), .out_2(demultiplexer_1_out_2),
    .out_3(demultiplexer_1_out_3), .out_4(demultiplexer_1_out_4));  // open: out_0, out_5, out_6, out_7, out_8, out_9, out_10, out_11, out_12, out_13, out_14, out_15
  and and_1 (and_1_out, demultiplexer_1_out_1, ctl__op__wsr);
  and and_2 (and_2_out, demultiplexer_1_out_2, ctl__op__wsr);
  and and_3 (and_3_out, demultiplexer_1_out_3, ctl__op__wsr);
  and and_4 (and_4_out, demultiplexer_1_out_4, ctl__op__wsr);
  Multiplexer #(.Bits(16)) multiplexer_1 (
    .sel(ctl__op__jal), .in_0({reg__port1__data_out, reg__port2__data_out}), .in_1(next__pc),
    .out(multiplexer_1_out));
  Multiplexer #(.Bits(16)) multiplexer_2 (
    .sel(ctl__wrflags), .in_0({reg__port1__data_out, reg__port2__data_out}),
    .in_1({{12{1'b0}}, alu__v, alu__n, alu__cout, alu__z}), .out(multiplexer_2_out));
  Multiplexer #(.Bits(16)) multiplexer_3 (
    .sel(ctl__op__halt), .in_0({reg__port1__data_out, reg__port2__data_out}), .in_1(hw__cause),
    .out(multiplexer_3_out));
  or or_1 (or_1_out, and_2_out, ctl__op__jal);
  or or_2 (or_2_out, and_3_out, ctl__wrflags);
  or or_3 (or_3_out, and_4_out, ctl__op__halt);
  Multiplexer #(.Bits(4)) multiplexer_4 (
    .sel(ctl__use__port3), .in_0(4'b0000), .in_1(decoder_1_dec__rs2), .out(multiplexer_4_out));
  decoder decoder_1 (
    .dec__inst(inst), .dec__op(decoder_1_dec__op), .dec__rd(decoder_1_dec__rd),
    .dec__rs1(decoder_1_dec__rs1), .dec__rs2(decoder_1_dec__rs2), .dec__imm(decoder_1_dec__imm),
    .dec__csr(decoder_1_dec__csr), .dec__cmp(decoder_1_dec__cmp));
  Multiplexer #(.Bits(4)) multiplexer_5 (
    .sel(ctl__use__port2), .in_0(4'b0000), .in_1(decoder_1_dec__rs1), .out(multiplexer_5_out));
  comparator comparator_1 (
    .cmp__flags({csrfile_1_csr__flags__out[15:2], flags__c, csrfile_1_csr__flags__out[0]}),
    .cmp__always(comparator_1_cmp__always), .cmp__equal(comparator_1_cmp__equal),
    .cmp__not__equal(comparator_1_cmp__not__equal), .cmp__greater(comparator_1_cmp__greater),
    .cmp__less(comparator_1_cmp__less), .cmp__greater__equal(comparator_1_cmp__greater__equal),
    .cmp__less__equal(comparator_1_cmp__less__equal));
  Multiplexer #(.Bits(4)) multiplexer_6 (
    .sel(ctl__use__port1), .in_0(4'b0000), .in_1(decoder_1_dec__rd), .out(multiplexer_6_out));
  Multiplexer #(.Bits(8)) multiplexer_7 (
    .sel(ctl__op__rsr), .in_0(reg__port1__data_in___alu), .in_1(reg__port1__data_in___rsr),
    .out(multiplexer_7_out));
  regfile regfile_1 (
    .reg__port1(multiplexer_6_out), .reg__port2(multiplexer_5_out), .reg__port3(multiplexer_4_out),
    .reg__port1__write(ctl__port1__write), .reg__port2__write(ctl__port2__write), .reg__clk(clk),
    .reg__port1__data_in(multiplexer_7_out), .reg__port2__data_in(reg__port2__data_in),
    .reg__port1__data_out(reg__port1__data_out), .reg__port2__data_out(reg__port2__data_out),
    .reg__port3__data(reg__port3__data));
  csrfile csrfile_1 (
    .csr__saddr__in({reg__port1__data_out, reg__port2__data_out}), .csr__raddr__in(multiplexer_1_out),
    .csr__flags__in(multiplexer_2_out), .csr__cause__in(multiplexer_3_out), .csr__saddr__write(and_1_out),
    .csr__raddr__write(or_1_out), .csr__flags__write(or_2_out), .csr__cause__write(or_3_out), .csr__clk(clk),
    .csr__saddr__out(csrfile_1_csr__saddr__out), .csr__raddr__out(csrfile_1_csr__raddr__out),
    .csr__flags__out({csrfile_1_csr__flags__out[15:2], flags__c, csrfile_1_csr__flags__out[0]}),
    .csr__cause__out(csrfile_1_csr__cause__out));  // open: csr__extns__out
  control control_1 (
    .ctl__stage(stage), .ctl__op(decoder_1_dec__op), .ctl__op__halt(ctl__op__halt),
    .ctl__op__add(ctl__op__add), .ctl__op__adc(ctl__op__adc), .ctl__op__sub(ctl__op__sub),
    .ctl__op__sbb(ctl__op__sbb), .ctl__op__and(ctl__op__and), .ctl__op__or(ctl__op__or),
    .ctl__op__xor(ctl__op__xor), .ctl__op__rrc(ctl__op__rcc), .ctl__op__set(ctl__op__set),
    .ctl__op__lw(ctl__op__lw), .ctl__op__sw(ctl__op__sw), .ctl__op__rsr(ctl__op__rsr),
    .ctl__op__wsr(ctl__op__wsr), .ctl__op__jal(ctl__op__jal), .ctl__op__jmp(ctl__op__jmp),
    .ctl__port1__write(ctl__port1__write), .ctl__port2__write(ctl__port2__write), .ctl__negb(ctl__negb),
    .ctl__add(ctl__add), .ctl__mem__wrback(ctl__mem__wrback), .ctl__mem__rdinst(ctl__mem__rdinst),
    .ctl__mem__read(ctl__mem__read), .ctl__mem__write(ctl__mem__write), .ctl__use__imm(ctl__use__imm),
    .ctl__use__port1(ctl__use__port1), .ctl__use__port2(ctl__use__port2), .ctl__use__port3(ctl__use__port3),
    .ctl__wrflags(ctl__wrflags), .ctl__branch(ctl__branch));
  Multiplexer #(.Selector_Bits(4)) multiplexer_8 (
    .sel(decoder_1_dec__cmp), .in_0(comparator_1_cmp__always), .in_1(comparator_1_cmp__equal),
    .in_2(comparator_1_cmp__greater), .in_3(comparator_1_cmp__greater__equal), .in_4(comparator_1_cmp__less),
    .in_5(comparator_1_cmp__less__equal), .in_6(1'b0), .in_7(1'b0), .in_8(comparator_1_cmp__not__equal),
    .in_9(1'b0), .in_10(1'b0), .in_11(1'b0), .in_12(1'b0), .in_13(1'b0), .in_14(1'b0), .in_15(1'b0),
    .out(cmp__branch));
  Multiplexer #(.Selector_Bits(4), .Bits(16)) multiplexer_9 (
    .sel(decoder_1_dec__csr), .in_0({16{1'b0}}), .in_1(csrfile_1_csr__saddr__out),
    .in_2(csrfile_1_csr__raddr__out),
    .in_3({csrfile_1_csr__flags__out[15:2], flags__c, csrfile_1_csr__flags__out[0]}),
    .in_4(csrfile_1_csr__cause__out), .in_5({16{1'b0}}), .in_6({16{1'b0}}), .in_7({16{1'b0}}),
    .in_8({16{1'b0}}), .in_9({16{1'b0}}), .in_10({16{1'b0}}), .in_11({16{1'b0}}), .in_12({16{1'b0}}),
    .in_13({16{1'b0}}), .in_14({16{1'b0}}), .in_15({16{1'b0}}),
    .out({reg__port1__data_in___rsr, reg__port2__data_in}));
  Multiplexer #(.Bits(16)) multiplexer_10 (
    .sel(Reset), .in_0(multiplexer_12_out), .in_1(16'hfff0), .out(multiplexer_10_out));
  JK_FF jk_ff_1 (.J(multiplexer_15_out), .C(clk), .K(1'b1), .Q(jk_ff_1_q));  // open: nQ
  Multiplexer #(.Bits(8)) multiplexer_11 (
    .sel(ctl__use__imm), .in_0(reg__port3__data), .in_1(decoder_1_dec__imm), .out(multiplexer_11_out));
  Multiplexer #(.Bits(16)) multiplexer_12 (
    .sel(and_5_out), .in_0(next__pc), .in_1({reg__port1__data_out, reg__port2__data_out}),
    .out(multiplexer_12_out));
  Register #(.Bits(16)) register_1 (.D(multiplexer_10_out), .C(clk), .en(1'b1), .Q(pc));
  Multiplexer multiplexer_13 (.sel(Reset), .in_0(jk_ff_1_q), .in_1(1'b0), .out(stage[0]));
  Demultiplexer #(.Selector_Bits(2), .Bits(8)) demultiplexer_2 (
    .sel(stage), .in(mem__read__data), .out_0(demultiplexer_2_out_0), .out_1(demultiplexer_2_out_1));  // open: out_2, out_3
  and and_5 (and_5_out, cmp__branch, ctl__branch);
  Multiplexer #(.Bits(16)) multiplexer_14 (
    .sel(stage__fetch), .in_0({16{1'b0}}), .in_1(16'h1), .out(multiplexer_14_out));
  Multiplexer multiplexer_15 (.sel(Reset), .in_0(jk_ff_2_nq), .in_1(1'b0), .out(multiplexer_15_out));
  Multiplexer #(.Selector_Bits(4)) multiplexer_16 (
    .sel(decoder_1_dec__op), .in_0(1'b0), .in_1(1'b0), .in_2(flags__c), .in_3(1'b1), .in_4(not_1_out),
    .in_5(1'b0), .in_6(1'b0), .in_7(1'b0), .in_8(1'b0), .in_9(1'b0), .in_10(1'b0), .in_11(1'b0),
    .in_12(1'b0), .in_13(1'b0), .in_14(1'b0), .in_15(1'b0), .out(multiplexer_16_out));
  not not_1 (not_1_out, flags__c);
  JK_FF jk_ff_2 (.J(stage[0]), .C(clk), .K(1'b1), .Q(stage[1]), .nQ(jk_ff_2_nq));
  Add #(.Bits(16)) add_1 (.a(pc), .b(multiplexer_14_out), .c_i(1'b0), .s(next__pc));  // open: c_o
  Register #(.Bits(8)) register_2 (.D(demultiplexer_2_out_0), .C(clk), .en(stage__fetchlo), .Q(inst[7:0]));
  Register #(.Bits(8)) register_3 (.D(demultiplexer_2_out_1), .C(clk), .en(stage__fetchhi), .Q(inst[15:8]));
  arithmetic arithmetic_1 (
    .alu__a(reg__port2__data_out), .alu__b(multiplexer_11_out), .alu__negb(ctl__negb),
    .alu__and(ctl__op__and), .alu__or(ctl__op__or), .alu__xor(ctl__op__xor), .alu__rot(ctl__op__rcc),
    .alu__cin(multiplexer_16_out), .alu__add(ctl__add), .alu__y(alu__y), .alu__z(alu__z),
    .alu__cout(alu__cout), .alu__n(alu__n), .alu__v(alu__v));
  not not_2 (not_2_out, halt);
  Demultiplexer #(.Selector_Bits(2)) demultiplexer_3 (
    .sel(stage), .in(1'b1), .out_0(stage__fetchlo), .out_1(stage__fetchhi), .out_2(stage__execute));  // open: out_3
  and and_6 (clk, Clock, not_2_out);
  RS_FF_AS rs_ff_as_1 (.S(ctl__op__halt), .R(Reset), .Q(rs_ff_as_1_q));  // open: nQ
  or or_4 (stage__fetch, stage__fetchhi, stage__fetchlo);
  Multiplexer #(.Bits(16)) multiplexer_17 (
    .sel(ctl__op__halt), .in_0({16{1'b0}}), .in_1({reg__port1__data_out, 8'h1}), .out(hw__cause));
  Multiplexer multiplexer_18 (.sel(halt), .in_0(clk), .in_1(Reset), .out(multiplexer_18_out));
  RS_FF rs_ff_1 (.S(rs_ff_as_1_q), .C(multiplexer_18_out), .R(Reset), .Q(halt));  // open: nQ
  Multiplexer #(.Bits(8)) multiplexer_19 (
    .sel(ctl__mem__wrback), .in_0(alu__y), .in_1(mem__read__data), .out(reg__port1__data_in___alu));
  Multiplexer #(.Bits(16)) multiplexer_20 (
    .sel(ctl__mem__rdinst), .in_0({reg__port2__data_out, reg__port3__data}), .in_1(pc),
    .out(multiplexer_20_out));
  memory memory_1 (
    .mem__write__data(reg__port1__data_out), .mem__addr(multiplexer_20_out), .mem__read(ctl__mem__read),
    .mem__write(ctl__mem__write), .mem__clk(clk), .mem__read__data(mem__read__data));  // open: mem__ready

  // Notes on the sheet:
  //   Clock: Hz: 2147483647
  //   Reset: default 1
  //   Register file
  //   Do-branch signal
  //   Control path
  //   CSR output
  //   ALU B generation
  //   Program counter
  //   Stage counter
  //   Instruction register
  //   Carry generation
  //   Clock
  //   Reset circuit
  //   Exception cause
  //   Stage signals
  //   Reg writeback generation
  //   Memory address generation
endmodule
