// Digital circuit misa8_3cpi_37pin.dig as structural Verilog
module misa8_3cpi_37pin (
  input  Clock,
  input  Reset,
  output [7:0] mem__write__data,
  output [15:0] mem__addr,
  output mem__read,
  output mem__write
);

  wire alu__cout, alu__n, alu__v, alu__z, and_1_out, and_2_out, and_3_out, and_4_out, and_5_out, and_6_out,
       and_7_out, clk, cmp__branch, comparator_1_cmp__always, comparator_1_cmp__equal,
       comparator_1_cmp__greater, comparator_1_cmp__greater__equal, comparator_1_cmp__less,
       comparator_1_cmp__less__equal, comparator_1_cmp__not__equal, ctl__add, ctl__branch,
       ctl__keep__loading__pc, ctl__load__pc, ctl__mem__rdinst, ctl__mem__wrback, ctl__negb, ctl__op__adc,
       ctl__op__add, ctl__op__and, ctl__op__halt, ctl__op__jal, ctl__op__jmp, ctl__op__ld, ctl__op__or,
       ctl__op__rcc, ctl__op__rsr, ctl__op__sbb, ctl__op__set, ctl__op__st, ctl__op__sub, ctl__op__wsr,
       ctl__op__xor, ctl__port1__write, ctl__port2__write, ctl__use__imm, ctl__use__port1, ctl__use__port2,
       ctl__use__port3, ctl__wrflags, d_ff_as_1_q, demultiplexer_1_out_1, demultiplexer_1_out_2,
       demultiplexer_1_out_3, demultiplexer_1_out_4, flags__c, halt, jk_ff_1_q, jk_ff_2_nq, loading__pc,
       mem__operation, mem__ready, multiplexer_11_out, multiplexer_15_out, not_1_out, or_1_out, or_2_out,
       or_3_out, stage__execute, stage__fetch, stage__fetchhi, stage__fetchlo;
  wire [1:0] stage;
  wire [3:0] decoder_1_dec__cmp, decoder_1_dec__csr, decoder_1_dec__op, decoder_1_dec__rd,
       decoder_1_dec__rs1, decoder_1_dec__rs2, multiplexer_4_out, multiplexer_5_out, multiplexer_6_out;
  wire [7:0] alu__y, decoder_1_dec__imm, demultiplexer_2_out_0, demultiplexer_2_out_1, mem__read__data,
       multiplexer_7_out, multiplexer_10_out, reg__port1__data_in___alu, reg__port1__data_in___rsr,
       reg__port2__data_in, reg__port2__data_out, reg__port3__data;
  wire [15:0] csrfile_1_csr__cause__out, csrfile_1_csr__flags__out, csrfile_1_csr__raddr__out,
       csrfile_1_csr__saddr__out, hw__cause, inst, multiplexer_1_out, multiplexer_2_out, multiplexer_3_out,
       multiplexer_12_out, multiplexer_16_out, multiplexer_17_out, next__pc, pc, register_1_q;

  Demultiplexer #(.Selector_Bits(4)) demultiplexer_1 (
    .sel(decoder_1_dec__csr), .in(1'b1), .out_1(demultiplexer_1_out_1), .out_2(demultiplexer_1_out_2),
    .out_3(demultiplexer_1_out_3), .out_4(demultiplexer_1_out_4));  // open: out_0, out_5, out_6, out_7, out_8, out_9, out_10, out_11, out_12, out_13, out_14, out_15
  and and_1 (and_1_out, demultiplexer_1_out_1, ctl__op__wsr);
  and and_2 (and_2_out, demultiplexer_1_out_2, ctl__op__wsr);
  and and_3 (and_3_out, demultiplexer_1_out_3, ctl__op__wsr);
  and and_4 (and_4_out, demultiplexer_1_out_4, ctl__op__wsr);
  Multiplexer #(.Bits(16)) multiplexer_1 (
    .sel(ctl__op__jal), .in_0({mem__write__data, reg__port2__data_out}), .in_1(next__pc),
    .out(multiplexer_1_out));
  Multiplexer #(.Bits(16)) multiplexer_2 (
    .sel(ctl__wrflags), .in_0({mem__write__data, reg__port2__data_out}),
    .in_1({{12{1'b0}}, alu__v, alu__n, alu__cout, alu__z}), .out(multiplexer_2_out));
  Multiplexer #(.Bits(16)) multiplexer_3 (
    .sel(ctl__op__halt), .in_0({mem__write__data, reg__port2__data_out}), .in_1(hw__cause),
    .out(multiplexer_3_out));
  or or_1 (or_1_out, and_2_out, ctl__op__jal);
  or or_2 (or_2_out, and_3_out, ctl__wrflags);
  or or_3 (or_3_out, and_4_out, ctl__op__halt);
  Multiplexer #(.Bits(4)) multiplexer_4 (
    .sel(ctl__use__port3), .in_0(4'b0000), .in_1(decoder_1_dec__rs2), .out(multiplexer_4_out));
  decoder decoder_1 (
    .dec__inst(inst), .dec__op(decoder_1_dec__op), .dec__rd(decoder_1_dec__rd),
    .dec__rs1(decoder_1_dec__rs1), .dec__rs2(decoder_1_dec__rs2), .dec__imm(decoder_1_dec__imm),
    .dec__csr(decoder_1_dec__csr), .dec__cmp(decoder_1_dec__cmp));
  Multiplexer #(.Bits(4)) multiplexer_5 (
    .sel(ctl__use__port2), .in_0(4'b0000), .in_1(decoder_1_dec__rs1), .out(multiplexer_5_out));
  comparator comparator_1 (
    .cmp__flags({csrfile_1_csr__flags__out[15:2], flags__c, csrfile_1_csr__flags__out[0]}),
    .cmp__always(comparator_1_cmp__always), .cmp__equal(comparator_1_cmp__equal),
    .cmp__not__equal(comparator_1_cmp__not__equal), .cmp__greater(comparator_1_cmp__greater),
    .cmp__less(comparator_1_cmp__less), .cmp__greater__equal(comparator_1_cmp__greater__equal),
    .cmp__less__equal(comparator_1_cmp__less__equal));
  Multiplexer #(.Bits(4)) multiplexer_6 (
    .sel(ctl__use__port1), .in_0(4'b0000), .in_1(decoder_1_dec__rd), .out(multiplexer_6_out));
  Multiplexer #(.Bits(8)) multiplexer_7 (
    .sel(ctl__op__rsr), .in_0(reg__port1__data_in___alu), .in_1(reg__port1__data_in___rsr),
    .out(multiplexer_7_out));
  regfile regfile_1 (
    .reg__port1(multiplexer_6_out), .reg__port2(multiplexer_5_out), .reg__port3(multiplexer_4_out),
    .reg__port1__write(ctl__port1__write), .reg__port2__write(ctl__port2__write), .reg__clk(clk),
    .reg__port1__data_in(multiplexer_7_out), .reg__port2__data_in(reg__port2__data_in),
    .reg__port1__data_out(mem__write__data), .reg__port2__data_out(reg__port2__data_out),
    .reg__port3__data(reg__port3__data));
  csrfile csrfile_1 (
    .csr__saddr__in({mem__write__data, reg__port2__data_out}), .csr__raddr__in(multiplexer_1_out),
    .csr__flags__in(multiplexer_2_out), .csr__cause__in(multiplexer_3_out), .csr__saddr__write(and_1_out),
    .csr__raddr__write(or_1_out), .csr__flags__write(or_2_out), .csr__cause__write(or_3_out), .csr__clk(clk),
    .csr__saddr__out(csrfile_1_csr__saddr__out), .csr__raddr__out(csrfile_1_csr__raddr__out),
    .csr__flags__out({csrfile_1_csr__flags__out[15:2], flags__c, csrfile_1_csr__flags__out[0]}),
    .csr__cause__out(csrfile_1_csr__cause__out));  // open: csr__extns__out
  Multiplexer #(.Selector_Bits(4)) multiplexer_8 (
    .sel(decoder_1_dec__cmp), .in_0(comparator_1_cmp__always), .in_1(comparator_1_cmp__equal),
    .in_2(comparator_1_cmp__greater), .in_3(comparator_1_cmp__greater__equal), .in_4(comparator_1_cmp__less),
    .in_5(comparator_1_cmp__less__equal), .in_6(1'b0), .in_7(1'b0), .in_8(comparator_1_cmp__not__equal),
    .in_9(1'b0), .in_10(1'b0), .in_11(1'b0), .in_12(1'b0), .in_13(1'b0), .in_14(1'b0), .in_15(1'b0),
    .out(cmp__branch));
  control control_1 (
    .ctl__stage(stage), .ctl__op(decoder_1_dec__op), .ctl__loading__pc(loading__pc),
    .ctl__op__halt(ctl__op__halt), .ctl__op__add(ctl__op__add), .ctl__op__adc(ctl__op__adc),
    .ctl__op__sub(ctl__op__sub), .ctl__op__sbb(ctl__op__sbb), .ctl__op__and(ctl__op__and),
    .ctl__op__or(ctl__op__or), .ctl__op__xor(ctl__op__xor), .ctl__op__rrc(ctl__op__rcc),
    .ctl__op__set(ctl__op__set), .ctl__op__ld(ctl__op__ld), .ctl__op__st(ctl__op__st),
    .ctl__op__rsr(ctl__op__rsr), .ctl__op__wsr(ctl__op__wsr), .ctl__op__jal(ctl__op__jal),
    .ctl__op__jmp(ctl__op__jmp), .ctl__port1__write(ctl__port1__write),
    .ctl__port2__write(ctl__port2__write), .ctl__negb(ctl__negb), .ctl__add(ctl__add),
    .ctl__mem__wrback(ctl__mem__wrback), .ctl__mem__rdinst(ctl__mem__rdinst), .ctl__mem__read(mem__read),
    .ctl__mem__write(mem__write), .ctl__use__imm(ctl__use__imm), .ctl__use__port1(ctl__use__port1),
    .ctl__use__port2(ctl__use__port2), .ctl__use__port3(ctl__use__port3), .ctl__wrflags(ctl__wrflags),
    .ctl__branch(ctl__branch), .ctl__load__pc(ctl__load__pc), .ctl__keep__loading__pc(ctl__keep__loading__pc));
  Multiplexer #(.Selector_Bits(4), .Bits(16)) multiplexer_9 (
    .sel(decoder_1_dec__csr), .in_0({16{1'b0}}), .in_1(csrfile_1_csr__saddr__out),
    .in_2(csrfile_1_csr__raddr__out),
    .in_3({csrfile_1_csr__flags__out[15:2], flags__c, csrfile_1_csr__flags__out[0]}),
    .in_4(csrfile_1_csr__cause__out), .in_5({16{1'b0}}), .in_6({16{1'b0}}), .in_7({16{1'b0}}),
    .in_8({16{1'b0}}), .in_9({16{1'b0}}), .in_10({16{1'b0}}), .in_11({16{1'b0}}), .in_12({16{1'b0}}),
    .in_13({16{1'b0}}), .in_14({16{1'b0}}), .in_15({16{1'b0}}),
    .out({reg__port1__data_in___rsr, reg__port2__data_in}));
  Multiplexer #(.Bits(8)) multiplexer_10 (
    .sel(ctl__use__imm), .in_0(reg__port3__data), .in_1(decoder_1_dec__imm), .out(multiplexer_10_out));
  Register #(.Bits(16)) register_1 (.D(multiplexer_12_out), .C(clk), .en(1'b1), .Q(register_1_q));
  JK_FF jk_ff_1 (.J(multiplexer_15_out), .C(clk), .K(1'b1), .Q(jk_ff_1_q));  // open: nQ
  Multiplexer #(.Selector_Bits(4)) multiplexer_11 (
    .sel(decoder_1_dec__op), .in_0(1'b0), .in_1(1'b0), .in_2(flags__c), .in_3(1'b1), .in_4(not_1_out),
    .in_5(1'b0), .in_6(1'b0), .in_7(1'b0), .in_8(1'b0), .in_9(1'b0), .in_10(1'b0), .in_11(1'b0),
    .in_12(1'b0), .in_13(1'b0), .in_14(1'b0), .in_15(1'b0), .out(multiplexer_11_out));
  not not_1 (not_1_out, flags__c);
  Multiplexer #(.Bits(16)) multiplexer_12 (
    .sel(ctl__load__pc), .in_0(multiplexer_16_out), .in_1(inst), .out(multiplexer_12_out));
  Multiplexer multiplexer_13 (.sel(Reset), .in_0(jk_ff_1_q), .in_1(1'b0), .out(stage[0]));
  Demultiplexer #(.Selector_Bits(2), .Bits(8)) demultiplexer_2 (
    .sel(stage), .in(mem__read__data), .out_0(demultiplexer_2_out_0), .out_1(demultiplexer_2_out_1));  // open: out_2, out_3
  Multiplexer #(.Bits(16)) multiplexer_14 (.sel(Reset), .in_0(register_1_q), .in_1(16'hfffd), .out(pc));
  Multiplexer multiplexer_15 (.sel(Reset), .in_0(jk_ff_2_nq), .in_1(1'b0), .out(multiplexer_15_out));
  Multiplexer #(.Bits(16)) multiplexer_16 (
    .sel(and_5_out), .in_0(next__pc), .in_1({mem__write__data, reg__port2__data_out}),
    .out(multiplexer_16_out));
  Add #(.Bits(16)) add_1 (.a(pc), .b(multiplexer_17_out), .c_i(1'b0), .s(next__pc));  // open: c_o
  JK_FF jk_ff_2 (.J(stage[0]), .C(clk), .K(1'b1), .Q(stage[1]), .nQ(jk_ff_2_nq));
  arithmetic arithmetic_1 (
    .alu__a(reg__port2__data_out), .alu__b(multiplexer_10_out), .alu__negb(ctl__negb),
    .alu__and(ctl__op__and), .alu__or(ctl__op__or), .alu__xor(ctl__op__xor), .alu__rot(ctl__op__rcc),
    .alu__cin(multiplexer_11_out), .alu__add(ctl__add), .alu__y(alu__y), .alu__z(alu__z),
    .alu__cout(alu__cout), .alu__n(alu__n), .alu__v(alu__v));
  and and_5 (and_5_out, cmp__branch, ctl__branch);
  Multiplexer #(.Bits(16)) multiplexer_17 (
    .sel(stage__fetch), .in_0({16{1'b0}}), .in_1(16'h1), .out(multiplexer_17_out));
  Register #(.Bits(8)) register_2 (.D(demultiplexer_2_out_0), .C(clk), .en(stage__fetchlo), .Q(inst[7:0]));
  Register #(.Bits(8)) register_3 (.D(demultiplexer_2_out_1), .C(clk), .en(stage__fetchhi), .Q(inst[15:8]));
  Demultiplexer #(.Selector_Bits(2)) demultiplexer_3 (
    .sel(stage), .in(1'b1), .out_0(stage__fetchlo), .out_1(stage__fetchhi), .out_2(stage__execute));  // open: out_3
  D_FF_AS d_ff_as_1 (.Set(1'b0), .D(ctl__op__halt), .C(clk), .Clr(Reset), .Q(d_ff_as_1_q));  // open: nQ
  or or_4 (stage__fetch, stage__fetchhi, stage__fetchlo);
  and and_6 (and_6_out, ~mem__ready, mem__operation);  // And
  or or_5 (halt, d_ff_as_1_q, and_7_out);
  and and_7 (and_7_out, halt, ~Reset);  // And
  Multiplexer #(.Bits(16)) multiplexer_18 (
    .sel(ctl__op__halt), .in_0({16{1'b0}}), .in_1({mem__write__data, 8'h1}), .out(hw__cause));
  Multiplexer #(.Bits(8)) multiplexer_19 (
    .sel(ctl__mem__wrback), .in_0(alu__y), .in_1(mem__read__data), .out(reg__port1__data_in___alu));
  Multiplexer #(.Bits(16)) multiplexer_20 (
    .sel(ctl__mem__rdinst), .in_0({reg__port2__data_out, reg__port3__data}), .in_1(pc), .out(mem__addr));
  and and_8 (clk, Clock, ~halt, ~and_6_out);  // And
  or or_6 (mem__operation, mem__read, mem__write);
  D_FF_AS d_ff_as_2 (.Set(Reset), .D(ctl__keep__loading__pc), .C(clk), .Clr(1'b0), .Q(loading__pc));  // open: nQ
  memory memory_1 (
    .mem__write__data(mem__write__data), .mem__addr(mem__addr), .mem__read(mem__read),
    .mem__write(mem__write), .mem__clk(clk), .mem__read__data(mem__read__data), .mem__ready(mem__ready));

  // Other names for the same wires on the sheet: ctl__mem__read = mem__read; ctl__mem__write = mem__write;
  //   reg__port1__data_out[7:0] = mem__write__data

  // Notes on the sheet:
  //   Clock: Hz: 5
  //   Reset: default 1
  //   Register file
  //   Do-branch signal
  //   Need a signal "loading init address" that persists for one full
  //   stage cycle (stages 0-2) after reset is released.
  //   This signal is passed to the control unit. When stage is 0-1, use
  //   0xFFF0 and 0xFFF1 as the PC value and load data into the
  //   instruction register as normal.
  //   When stage = 2 and the "loading init address" signal is high,
  //   control unit will not execute any instruction, and will instead emit
  //   a signal that tells the PC circuit to load the value from the
  //   instruction register into the PC.
  //   From there, the "loading init address" signal should go low, and
  //   the processor state machine can proceed as normal.
  //   Control path
  //   CSR output
  //   ALU B generation
  //   Carry generation
  //   Stage counter
  //   Instruction register
  //   Reset circuit:
  //   - Signal that persists until stage 0-2 passes for the first time
  //   PC circuit:
  //   - Emit 0xFFF0 as the initial PC value when reset is asserted
  //   - Increment to 0xFFF1 as normal for stage 1
  //   - Mux controlled by control unit signal that sets PC value based on inst
  //   Control unit:
  //   - Take "loading init address" as an input signal
  //   - Keep everything (e.g. all the ctl\_op signals) low if loading init address
  //   - On stage 2, emit the PC control signal to load inst into the PC
  //   - It might be easiest to have the control unit emit a new "loading init
  //     address" signal. When stage = 2, emit low, which keeps it low forever.
  //     Setting reset will reset this signal to high
  //   Clock
  //   Reset circuit
  //   Exception cause
  //   Stage signals
  //   Reg writeback generation
  //   Memory address generation
endmodule
