// Digital circuit misa8_3cpi_37pin_package.dig as structural Verilog
module misa8_3cpi_37pin_package (
  input  Clock,
  input  Reset
);

  wire memory_1_mem__ready, misa8_3cpi_37pin_1_mem__read, misa8_3cpi_37pin_1_mem__write;
  wire [7:0] memory_1_mem__read__data, misa8_3cpi_37pin_1_mem__write__data;
  wire [15:0] misa8_3cpi_37pin_1_mem__addr;

  misa8_3cpi_37pin misa8_3cpi_37pin_1 (
    .Clock(Clock), .Reset(Reset), .mem__read__data(memory_1_mem__read__data),
    .mem__ready(memory_1_mem__ready), .mem__write__data(misa8_3cpi_37pin_1_mem__write__data),
    .mem__addr(misa8_3cpi_37pin_1_mem__addr), .mem__read(misa8_3cpi_37pin_1_mem__read),
    .mem__write(misa8_3cpi_37pin_1_mem__write));
  memory memory_1 (
    .mem__write__data(misa8_3cpi_37pin_1_mem__write__data), .mem__addr(misa8_3cpi_37pin_1_mem__addr),
    .mem__read(misa8_3cpi_37pin_1_mem__read), .mem__write(misa8_3cpi_37pin_1_mem__write), .mem__clk(Clock),
    .mem__read__data(memory_1_mem__read__data), .mem__ready(memory_1_mem__ready));

  // Notes on the sheet:
  //   Clock: Hz: 10
  //   Reset: default 1
endmodule
